# Fritzing sketch dac-rpi (saved by Fritzing 1.0.5)
breadboards: 1

parts:
  A1 = Raspberry Pi 5  # not connected
  A2 = Pcm5102A module

nets:
  N1: A2.Pin_8, A2.Pin_9, A2.Pin_10, A2.Pin_11, A2.Pin_12

custom parts:
  Raspberry Pi 5: The RPi5, a faster version of the awesome Raspberry Pi4B ARM Board with 40 pin gpio.
  Pcm5102A module: Interface I2S PCM5102A DAC Decoder GY-PCM5102 I2S Player Module for Raspberry Pi pHAT Format Board Digital PCM5102 Audio Board.
